# Fritzing sketch 17_BMP280_16x2_LCD (saved by Fritzing 0.9.3b)
breadboards: 1

parts:
  Bauteil2 = Barometric Pressure Sensor - BMP085 Breakout
  Bauteil3 = Arduino Nano (Rev3.0)
  Bauteil4 = LCD1602-I2C

nets:
  N1: Bauteil2.SCL, Bauteil3.GND, Bauteil3.D3, Bauteil3.D9, Bauteil4.SCL
  N2: Bauteil2.SDA, Bauteil4.SDA
  N3: Bauteil3.D1/TX, Bauteil3.A2, Bauteil4.VCC

custom parts:
  LCD1602-I2C: A standard character display, usually with 2x16 characters. Comes in many colors with LCM1602 IIC attached.
